// Logisim project logicaBranch.circ as structural Verilog: 1 circuit, main circuit main
module main (
  input  [4:0] Offset
);

  wire [7:0] adder_1_out, bit_extender_1_out, multiplexer_1_out, subtractor_2_out;

  Subtractor subtractor_1 ();  // open: a, b, out, bin, bout
  assign bit_extender_1_out = {{4{1'b0}}, Offset[3:0]};  // Bit_Extender bit_extender_1
  Adder adder_1 (.a(8'h3), .b(bit_extender_1_out), .out(adder_1_out));  // open: cin, cout
  Multiplexer #(.width(8), .enable("false")) multiplexer_1 (
    .in0(adder_1_out), .in1(subtractor_2_out), .out(multiplexer_1_out), .sel(Offset[4]));
  Subtractor subtractor_2 (.a(8'h3), .b(bit_extender_1_out), .out(subtractor_2_out));  // open: bin, bout
  // Probe on multiplexer_1_out

  // Notes on the sheet:
  //   Solo para en branch
  //   PC ya incrementado
endmodule
