// Logisim project ProyectoMIPS.circ as structural Verilog: 16 circuits, main circuit main
// address
module main (
  input  Active_Store,
  input  Reset,
  input  [31:0] in_3,
  output [31:0] out_4
);

  wire AluSrc, Branch, clock, clock_2_out, letter_1_out_2, letter_1_out_3, letter_1_out_4, letter_1_out_5,
       letter_1_out_6, letter_1_out_7, letter_1_out_8, letter_2_out_2, letter_2_out_3, letter_2_out_4,
       letter_2_out_5, letter_2_out_6, letter_2_out_7, letter_2_out_8, letter_3_out_2, letter_3_out_3,
       letter_3_out_4, letter_3_out_5, letter_3_out_6, letter_3_out_7, letter_3_out_8, MemReed, MemToReg,
       Memwrite, num_1_out_2, num_1_out_3, num_1_out_4, num_1_out_5, num_1_out_6, num_1_out_7, num_1_out_8,
       num_2_out_2, num_2_out_3, num_2_out_4, num_2_out_5, num_2_out_6, num_2_out_7, num_2_out_8,
       num_3_out_2, num_3_out_3, num_3_out_4, num_3_out_5, num_3_out_6, num_3_out_7, num_3_out_8,
       num_4_out_2, num_4_out_3, num_4_out_4, num_4_out_5, num_4_out_6, num_4_out_7, num_4_out_8,
       num_5_out_2, num_5_out_3, num_5_out_4, num_5_out_5, num_5_out_6, num_5_out_7, num_5_out_8,
       num_6_out_2, num_6_out_3, num_6_out_4, num_6_out_5, num_6_out_6, num_6_out_7, num_6_out_8,
       num_7_out_2, num_7_out_3, num_7_out_4, num_7_out_5, num_7_out_6, num_7_out_7, num_7_out_8,
       num_8_out_2, num_8_out_3, num_8_out_4, num_8_out_5, num_8_out_6, num_8_out_7, num_8_out_8,
       num_9_out_2, num_9_out_3, num_9_out_4, num_9_out_5, num_9_out_6, num_9_out_7, num_9_out_8,
       num_10_out_2, num_10_out_3, num_10_out_4, num_10_out_5, num_10_out_6, num_10_out_7, num_10_out_8,
       num_11_out_2, num_11_out_3, num_11_out_4, num_11_out_5, num_11_out_6, num_11_out_7, num_11_out_8,
       num_12_out_2, num_12_out_3, num_12_out_4, num_12_out_5, num_12_out_6, num_12_out_7, num_12_out_8,
       num_13_out_2, num_13_out_3, num_13_out_4, num_13_out_5, num_13_out_6, num_13_out_7, num_13_out_8,
       num_14_out_2, num_14_out_3, num_14_out_4, num_14_out_5, num_14_out_6, num_14_out_7, num_14_out_8,
       num_15_out_2, num_15_out_3, num_15_out_4, num_15_out_5, num_15_out_6, num_15_out_7, num_15_out_8,
       or_1_out, or_2_out, rd0, rd1, rd2, rd3, rd4, RegDist, RegWrite, Reset_out, rs0, rs1, rs2, rs3, rs4,
       rt0, rt1, rt2, rt3, rt4;
  wire [1:0] aluop;
  wire [2:0] alu_control_1_out_3;
  wire [3:0] bit_extender_1_out, bit_extender_2_out;
  wire [4:0] decode_1_rd, decode_1_rs, decode_1_rt;
  wire [5:0] decode_1_dibujado, funct, Opcode;
  wire [6:0] s1, s2, s3;
  wire [15:0] address;
  wire [23:0] adder_1_out, register_1_q;
  wire [25:0] addressJ;
  wire [31:0] dalu, Dato1, Dato2, dreg, multiplexer_2_out;

  Register_part #(.width(24)) register_1 (.D(adder_1_out), .Q(register_1_q), .clk(clock), .clr(Reset_out));  // open: en
  Button u_Reset (.out(Reset_out));
  Adder #(.width(24)) adder_1 (.a(register_1_q), .b(24'h1), .out(adder_1_out));  // open: cin, cout
  Clock clock_1 (.out(clock));
  RAM #(.addrWidth(24), .dataWidth(32), .bus("separate")) ram_1 (
    .addr(register_1_q), .din(in_3), .data(out_4), .str(Active_Store), .clk(clock), .ld(1'b1), .clr(Reset));  // open: sel
  Decode decode_1 (
    .in_1(out_4), .Address_J(addressJ), .Address(address), .rs(decode_1_rs), .rt(decode_1_rt),
    .rd(decode_1_rd), .Dibujado(decode_1_dibujado), .funct(funct), .Op(Opcode));  // open: Shamt
  ShowOp_funct showop_funct_1 (.Funct_0p(decode_1_dibujado), .s1(s1), .s2(s2), .s2_2(s3));
  Register register_2 (
    .rs(decode_1_rs), .in_rd(dalu), .rt(decode_1_rt), .rd(decode_1_rt), .output_rs(Dato1), .output_rt(Dato2));
  Penilla penilla_1 (.Input(decode_1_rs), .s0(rs0), .s1(rs1), .s2(rs2), .s3(rs3), .s4(rs4));
  Penilla penilla_2 (.Input(decode_1_rt), .s0(rt0), .s1(rt1), .s2(rt2), .s3(rt3), .s4(rt4));
  Penilla penilla_3 (.Input(decode_1_rd), .s0(rd0), .s1(rd1), .s2(rd2), .s3(rd3), .s4(rd4));
  Unidad_Control unidad_control_1 (
    .op_in(Opcode), .RegDist(RegDist), .ALUSrc(AluSrc), .MemToReg(MemToReg), .RegWrite(RegWrite),
    .MemReed(MemReed), .MemWrite(Memwrite), .Branch(Branch), .AluOP(aluop));
  ALU alu_1 (.Dato1(Dato1), .Output(dalu), .Dato2(Dato2), .Opcode(bit_extender_1_out));  // open: C, V
  ALU_Control alu_control_1 (.funct(funct), .in_1(aluop), .out_3(alu_control_1_out_3));
  assign bit_extender_1_out = {{1{1'b0}}, alu_control_1_out_3};  // Bit_Extender bit_extender_1
  Multiplexer #(.width(32), .enable("false")) multiplexer_1 (.in1(dalu), .out(dreg), .sel(Memwrite));  // open: in0
  or or_1 (or_1_out, MemReed, Memwrite);
  _7_Segment_Display u_7_segment_display_1 (
    .g(letter_1_out_5), .f(letter_1_out_4), .a(letter_1_out_3), .b(letter_1_out_2), .e(letter_1_out_8),
    .d(letter_1_out_7), .c(letter_1_out_6));  // open: dp
  Letter letter_1 (
    .Number(s1), .out_8(letter_1_out_8), .out_7(letter_1_out_7), .out_6(letter_1_out_6),
    .out_5(letter_1_out_5), .out_4(letter_1_out_4), .out_3(letter_1_out_3), .out_2(letter_1_out_2));
  _7_Segment_Display u_7_segment_display_2 (
    .g(num_1_out_5), .f(num_1_out_4), .a(num_1_out_3), .b(num_1_out_2), .e(num_1_out_8), .d(num_1_out_7),
    .c(num_1_out_6));  // open: dp
  num num_1 (
    .in_1(rs0), .out_8(num_1_out_8), .out_7(num_1_out_7), .out_6(num_1_out_6), .out_5(num_1_out_5),
    .out_4(num_1_out_4), .out_3(num_1_out_3), .out_2(num_1_out_2));
  _7_Segment_Display u_7_segment_display_3 (
    .g(num_2_out_5), .f(num_2_out_4), .a(num_2_out_3), .b(num_2_out_2), .e(num_2_out_8), .d(num_2_out_7),
    .c(num_2_out_6));  // open: dp
  num num_2 (
    .in_1(rt0), .out_8(num_2_out_8), .out_7(num_2_out_7), .out_6(num_2_out_6), .out_5(num_2_out_5),
    .out_4(num_2_out_4), .out_3(num_2_out_3), .out_2(num_2_out_2));
  _7_Segment_Display u_7_segment_display_4 (
    .g(num_3_out_5), .f(num_3_out_4), .a(num_3_out_3), .b(num_3_out_2), .e(num_3_out_8), .d(num_3_out_7),
    .c(num_3_out_6));  // open: dp
  num num_3 (
    .in_1(rd0), .out_8(num_3_out_8), .out_7(num_3_out_7), .out_6(num_3_out_6), .out_5(num_3_out_5),
    .out_4(num_3_out_4), .out_3(num_3_out_3), .out_2(num_3_out_2));
  RAM #(.addrWidth(24), .dataWidth(32)) ram_2 (
    .addr(dalu[23:0]), .data(dreg), .sel(or_1_out), .clk(clock), .ld(MemReed));  // open: clr
  _7_Segment_Display u_7_segment_display_5 (
    .g(letter_2_out_5), .f(letter_2_out_4), .a(letter_2_out_3), .b(letter_2_out_2), .e(letter_2_out_8),
    .d(letter_2_out_7), .c(letter_2_out_6));  // open: dp
  Letter letter_2 (
    .Number(s2), .out_8(letter_2_out_8), .out_7(letter_2_out_7), .out_6(letter_2_out_6),
    .out_5(letter_2_out_5), .out_4(letter_2_out_4), .out_3(letter_2_out_3), .out_2(letter_2_out_2));
  _7_Segment_Display u_7_segment_display_6 (
    .g(num_4_out_5), .f(num_4_out_4), .a(num_4_out_3), .b(num_4_out_2), .e(num_4_out_8), .d(num_4_out_7),
    .c(num_4_out_6));  // open: dp
  num num_4 (
    .in_1(rs1), .out_8(num_4_out_8), .out_7(num_4_out_7), .out_6(num_4_out_6), .out_5(num_4_out_5),
    .out_4(num_4_out_4), .out_3(num_4_out_3), .out_2(num_4_out_2));
  _7_Segment_Display u_7_segment_display_7 (
    .g(num_5_out_5), .f(num_5_out_4), .a(num_5_out_3), .b(num_5_out_2), .e(num_5_out_8), .d(num_5_out_7),
    .c(num_5_out_6));  // open: dp
  num num_5 (
    .in_1(rt1), .out_8(num_5_out_8), .out_7(num_5_out_7), .out_6(num_5_out_6), .out_5(num_5_out_5),
    .out_4(num_5_out_4), .out_3(num_5_out_3), .out_2(num_5_out_2));
  _7_Segment_Display u_7_segment_display_8 (
    .g(num_6_out_5), .f(num_6_out_4), .a(num_6_out_3), .b(num_6_out_2), .e(num_6_out_8), .d(num_6_out_7),
    .c(num_6_out_6));  // open: dp
  num num_6 (
    .in_1(rd1), .out_8(num_6_out_8), .out_7(num_6_out_7), .out_6(num_6_out_6), .out_5(num_6_out_5),
    .out_4(num_6_out_4), .out_3(num_6_out_3), .out_2(num_6_out_2));
  _7_Segment_Display u_7_segment_display_9 (
    .g(letter_3_out_5), .f(letter_3_out_4), .a(letter_3_out_3), .b(letter_3_out_2), .e(letter_3_out_8),
    .d(letter_3_out_7), .c(letter_3_out_6));  // open: dp
  Letter letter_3 (
    .Number(s3), .out_8(letter_3_out_8), .out_7(letter_3_out_7), .out_6(letter_3_out_6),
    .out_5(letter_3_out_5), .out_4(letter_3_out_4), .out_3(letter_3_out_3), .out_2(letter_3_out_2));
  _7_Segment_Display u_7_segment_display_10 (
    .g(num_7_out_5), .f(num_7_out_4), .a(num_7_out_3), .b(num_7_out_2), .e(num_7_out_8), .d(num_7_out_7),
    .c(num_7_out_6));  // open: dp
  num num_7 (
    .in_1(rs2), .out_8(num_7_out_8), .out_7(num_7_out_7), .out_6(num_7_out_6), .out_5(num_7_out_5),
    .out_4(num_7_out_4), .out_3(num_7_out_3), .out_2(num_7_out_2));
  _7_Segment_Display u_7_segment_display_11 (
    .g(num_8_out_5), .f(num_8_out_4), .a(num_8_out_3), .b(num_8_out_2), .e(num_8_out_8), .d(num_8_out_7),
    .c(num_8_out_6));  // open: dp
  num num_8 (
    .in_1(rt2), .out_8(num_8_out_8), .out_7(num_8_out_7), .out_6(num_8_out_6), .out_5(num_8_out_5),
    .out_4(num_8_out_4), .out_3(num_8_out_3), .out_2(num_8_out_2));
  _7_Segment_Display u_7_segment_display_12 (
    .g(num_9_out_5), .f(num_9_out_4), .a(num_9_out_3), .b(num_9_out_2), .e(num_9_out_8), .d(num_9_out_7),
    .c(num_9_out_6));  // open: dp
  num num_9 (
    .in_1(rd2), .out_8(num_9_out_8), .out_7(num_9_out_7), .out_6(num_9_out_6), .out_5(num_9_out_5),
    .out_4(num_9_out_4), .out_3(num_9_out_3), .out_2(num_9_out_2));
  _7_Segment_Display u_7_segment_display_13 (
    .g(num_10_out_5), .f(num_10_out_4), .a(num_10_out_3), .b(num_10_out_2), .e(num_10_out_8),
    .d(num_10_out_7), .c(num_10_out_6));  // open: dp
  num num_10 (
    .in_1(rs3), .out_8(num_10_out_8), .out_7(num_10_out_7), .out_6(num_10_out_6), .out_5(num_10_out_5),
    .out_4(num_10_out_4), .out_3(num_10_out_3), .out_2(num_10_out_2));
  _7_Segment_Display u_7_segment_display_14 (
    .g(num_11_out_5), .f(num_11_out_4), .a(num_11_out_3), .b(num_11_out_2), .e(num_11_out_8),
    .d(num_11_out_7), .c(num_11_out_6));  // open: dp
  num num_11 (
    .in_1(rt3), .out_8(num_11_out_8), .out_7(num_11_out_7), .out_6(num_11_out_6), .out_5(num_11_out_5),
    .out_4(num_11_out_4), .out_3(num_11_out_3), .out_2(num_11_out_2));
  _7_Segment_Display u_7_segment_display_15 (
    .g(num_12_out_5), .f(num_12_out_4), .a(num_12_out_3), .b(num_12_out_2), .e(num_12_out_8),
    .d(num_12_out_7), .c(num_12_out_6));  // open: dp
  num num_12 (
    .in_1(rd3), .out_8(num_12_out_8), .out_7(num_12_out_7), .out_6(num_12_out_6), .out_5(num_12_out_5),
    .out_4(num_12_out_4), .out_3(num_12_out_3), .out_2(num_12_out_2));
  _7_Segment_Display u_7_segment_display_16 (
    .g(num_13_out_5), .f(num_13_out_4), .a(num_13_out_3), .b(num_13_out_2), .e(num_13_out_8),
    .d(num_13_out_7), .c(num_13_out_6));  // open: dp
  num num_13 (
    .in_1(rs4), .out_8(num_13_out_8), .out_7(num_13_out_7), .out_6(num_13_out_6), .out_5(num_13_out_5),
    .out_4(num_13_out_4), .out_3(num_13_out_3), .out_2(num_13_out_2));
  _7_Segment_Display u_7_segment_display_17 (
    .g(num_14_out_5), .f(num_14_out_4), .a(num_14_out_3), .b(num_14_out_2), .e(num_14_out_8),
    .d(num_14_out_7), .c(num_14_out_6));  // open: dp
  num num_14 (
    .in_1(rt4), .out_8(num_14_out_8), .out_7(num_14_out_7), .out_6(num_14_out_6), .out_5(num_14_out_5),
    .out_4(num_14_out_4), .out_3(num_14_out_3), .out_2(num_14_out_2));
  _7_Segment_Display u_7_segment_display_18 (
    .g(num_15_out_5), .f(num_15_out_4), .a(num_15_out_3), .b(num_15_out_2), .e(num_15_out_8),
    .d(num_15_out_7), .c(num_15_out_6));  // open: dp
  num num_15 (
    .in_1(rd4), .out_8(num_15_out_8), .out_7(num_15_out_7), .out_6(num_15_out_6), .out_5(num_15_out_5),
    .out_4(num_15_out_4), .out_3(num_15_out_3), .out_2(num_15_out_2));
  or or_2 (or_2_out, Memwrite, MemReed);
  Clock clock_2 (.out(clock_2_out));
  RAM #(.addrWidth(24), .dataWidth(32)) ram_3 (
    .addr(dalu[23:0]), .data(dalu), .sel(or_2_out), .clk(clock_2_out), .ld(MemReed));  // open: clr
  Hex_Digit_Display hex_digit_display_1 (.value(bit_extender_2_out));  // open: dp
  assign bit_extender_2_out = {{2{1'b0}}, addressJ[25:24]};  // Bit_Extender bit_extender_2
  Hex_Digit_Display hex_digit_display_2 (.value(addressJ[23:20]));  // open: dp
  Hex_Digit_Display hex_digit_display_3 (.value(addressJ[19:16]));  // open: dp
  Hex_Digit_Display hex_digit_display_4 (.value(address[15:12]));  // open: dp
  Hex_Digit_Display hex_digit_display_5 (.value(address[11:8]));  // open: dp
  Multiplexer #(.width(32), .enable("false")) multiplexer_2 (
    .in0(dalu), .in1(dalu), .out(multiplexer_2_out), .sel(Memwrite));
  Hex_Digit_Display hex_digit_display_6 (.value(addressJ[15:12]));  // open: dp
  Hex_Digit_Display hex_digit_display_7 (.value(addressJ[11:8]));  // open: dp
  Hex_Digit_Display hex_digit_display_8 (.value(address[7:4]));  // open: dp
  Hex_Digit_Display hex_digit_display_9 (.value(address[3:0]));  // open: dp
  Hex_Digit_Display hex_digit_display_10 (.value(addressJ[3:0]));  // open: dp
  Hex_Digit_Display hex_digit_display_11 (.value(addressJ[7:4]));  // open: dp

  // Other names for the same wires on the sheet: result[31:0] = dalu

  // Notes on the sheet:
  //   FETCH
  //   Active load
  //   RS
  //   RT
  //   Operacion
  //   RD
  //   AddressJump:
  //   Address:
endmodule

module PC (
  input  Clock,
  input  Reset,
  output [23:0] Address
);

  wire [23:0] adder_1_out;

  Adder #(.width(24)) adder_1 (.a(Address), .b(24'h1), .out(adder_1_out));  // open: cin, cout
  Register_part #(.width(24)) register_1 (.D(adder_1_out), .Q(Address), .clk(Clock), .clr(Reset));  // open: en
endmodule

module Decode (
  input  [31:0] in_1,
  output [25:0] Address_J,
  output [15:0] Address,
  output [4:0] rs,
  output [4:0] rt,
  output [4:0] rd,
  output [4:0] Shamt,
  output [5:0] Dibujado,
  output [5:0] funct,
  output [5:0] Op
);

  wire not_1_out;
  wire [1:0] comparator_2_eq;
  wire [25:0] demultiplexer_1_out0;
  wire [25:16] demultiplexer_1_out1;

  Comparator #(.width(6)) comparator_1 (.a(in_1[31:26]), .b({6{1'b0}}), .eq(comparator_2_eq[1]));  // open: gt, lt
  Demultiplexer #(.width(26), .enable("false")) demultiplexer_1 (
    .out0(demultiplexer_1_out0), .out1({demultiplexer_1_out1, rd, Shamt, funct}), .in(in_1[25:0]),
    .sel(comparator_2_eq[1]));
  Comparator #(.width(6)) comparator_2 (.a(in_1[31:26]), .b(6'b000010), .eq(comparator_2_eq[0]));  // open: gt, lt
  Multiplexer #(.width(6), .enable("false")) multiplexer_1 (
    .in0(funct), .in1(in_1[31:26]), .out(Dibujado), .sel(not_1_out));
  not not_1 (not_1_out, comparator_2_eq[1]);
  Multiplexer #(.width(16), .enable("false")) multiplexer_2 (
    .in0(demultiplexer_1_out0[15:0]), .in1({16{1'b0}}), .out(Address), .sel(comparator_2_eq[0]));
  Multiplexer #(.width(26), .enable("false")) multiplexer_3 (
    .in0({26{1'b0}}), .in1(demultiplexer_1_out0), .out(Address_J), .sel(comparator_2_eq[0]));
  Multiplexer #(.select(2), .width(10), .enable("false")) multiplexer_4 (
    .in0(demultiplexer_1_out0[25:16]), .in1({10{1'b0}}), .in2(demultiplexer_1_out1), .out({rs, rt}),
    .sel(comparator_2_eq));  // open: in3

  assign Op = in_1[31:26];
endmodule

module Penilla (
  input  [4:0] Input,
  output s0,
  output s1,
  output s2,
  output s3,
  output s4
);


  assign s0 = Input[0];
  assign s1 = Input[1];
  assign s2 = Input[2];
  assign s3 = Input[3];
  assign s4 = Input[4];
endmodule

module num (
  input  in_1,
  output out_2,
  output out_3,
  output out_4,
  output out_5,
  output out_6,
  output out_7,
  output out_8
);

  Multiplexer #(.width(7), .enable("false")) multiplexer_1 (
    .in0(7'b1110111), .in1(7'b0010001), .out({out_8, out_7, out_6, out_5, out_4, out_3, out_2}), .sel(in_1));
endmodule

module ShowOp_funct (
  input  [5:0] Funct_0p,
  output [6:0] s1,
  output [6:0] s2,
  output [6:0] s2_2
);

  wire comparator_1_eq, comparator_2_eq, comparator_3_eq, comparator_4_eq, comparator_5_eq, comparator_6_eq,
       comparator_7_eq, comparator_8_eq, comparator_9_eq, comparator_10_eq, letter_1_out_2, letter_1_out_3,
       letter_1_out_4, letter_1_out_5, letter_1_out_6, letter_1_out_7, letter_1_out_8, letter_2_out_2,
       letter_2_out_3, letter_2_out_4, letter_2_out_5, letter_2_out_6, letter_2_out_7, letter_2_out_8,
       letter_3_out_2, letter_3_out_3, letter_3_out_4, letter_3_out_5, letter_3_out_6, letter_3_out_7,
       letter_3_out_8;
  wire [3:0] opchooser_1_s0;

  Comparator #(.width(6)) comparator_1 (.a(Funct_0p), .b(6'b100000), .eq(comparator_1_eq));  // open: gt, lt
  Comparator #(.width(6)) comparator_2 (.a(Funct_0p), .b(6'b100010), .eq(comparator_2_eq));  // open: gt, lt
  Comparator #(.width(6)) comparator_3 (.a(Funct_0p), .b(6'b100100), .eq(comparator_3_eq));  // open: gt, lt
  Comparator #(.width(6)) comparator_4 (.a(Funct_0p), .b(6'b100101), .eq(comparator_4_eq));  // open: gt, lt
  Comparator #(.width(6)) comparator_5 (.a(Funct_0p), .b(6'b011000), .eq(comparator_5_eq));  // open: gt, lt
  Comparator #(.width(6)) comparator_6 (.a(Funct_0p), .b(6'b000100), .eq(comparator_6_eq));  // open: gt, lt
  Comparator #(.width(6)) comparator_7 (.a(Funct_0p), .b(6'b000010), .eq(comparator_7_eq));  // open: gt, lt
  Comparator #(.width(6)) comparator_8 (.a(Funct_0p), .b(6'b100011), .eq(comparator_8_eq));  // open: gt, lt
  Comparator #(.width(6)) comparator_9 (.a(Funct_0p), .b(6'b110011), .eq(comparator_9_eq));  // open: gt, lt
  Comparator #(.width(6)) comparator_10 (.a(Funct_0p), .b(6'b001000), .eq(comparator_10_eq));  // open: gt, lt
  OpChooser opchooser_1 (
    .add(comparator_1_eq), .sub(comparator_2_eq), .\and (comparator_3_eq), .\or (comparator_4_eq),
    .mult(comparator_5_eq), .beq(comparator_6_eq), .jump(comparator_7_eq), .load(comparator_8_eq),
    .store(comparator_9_eq), .addi(comparator_10_eq), .s3(opchooser_1_s0[3]), .s2(opchooser_1_s0[2]),
    .s1(opchooser_1_s0[1]), .s0(opchooser_1_s0[0]));
  Multiplexer #(.select(4), .width(21), .enable("false")) multiplexer_1 (
    .in0(21'h20408), .in1(21'h1e7cdf), .in2(21'h1f3abe), .in3(21'h1e6bdf), .in4(21'h133b88),
    .in5(21'h113ad7), .in6(21'h7f7fc), .in7(21'h15faf1), .in8(21'h1d7ae4), .in9(21'h1d7abe),
    .in10(21'h113cdf), .out({s2_2, s2, s1}), .sel(opchooser_1_s0));  // open: in11, in12, in13, in14, in15
  _7_Segment_Display u_7_segment_display_1 (
    .g(letter_1_out_5), .f(letter_1_out_4), .a(letter_1_out_3), .b(letter_1_out_2), .e(letter_1_out_8),
    .d(letter_1_out_7), .c(letter_1_out_6));  // open: dp
  Letter letter_1 (
    .Number(s1), .out_8(letter_1_out_8), .out_7(letter_1_out_7), .out_6(letter_1_out_6),
    .out_5(letter_1_out_5), .out_4(letter_1_out_4), .out_3(letter_1_out_3), .out_2(letter_1_out_2));
  _7_Segment_Display u_7_segment_display_2 (
    .g(letter_2_out_5), .f(letter_2_out_4), .a(letter_2_out_3), .b(letter_2_out_2), .e(letter_2_out_8),
    .d(letter_2_out_7), .c(letter_2_out_6));  // open: dp
  Letter letter_2 (
    .Number(s2), .out_8(letter_2_out_8), .out_7(letter_2_out_7), .out_6(letter_2_out_6),
    .out_5(letter_2_out_5), .out_4(letter_2_out_4), .out_3(letter_2_out_3), .out_2(letter_2_out_2));
  _7_Segment_Display u_7_segment_display_3 (
    .g(letter_3_out_5), .f(letter_3_out_4), .a(letter_3_out_3), .b(letter_3_out_2), .e(letter_3_out_8),
    .d(letter_3_out_7), .c(letter_3_out_6));  // open: dp
  Letter letter_3 (
    .Number(s2_2), .out_8(letter_3_out_8), .out_7(letter_3_out_7), .out_6(letter_3_out_6),
    .out_5(letter_3_out_5), .out_4(letter_3_out_4), .out_3(letter_3_out_3), .out_2(letter_3_out_2));

  // Other names for the same wires on the sheet: s3[6:0] = s2_2

  // Notes on the sheet:
  //   Add
  //   Sub
  //   And
  //   or
  //   Mult
  //   Beq
  //   jum
  //   load
  //   store
  //   addi
endmodule

module Letter (
  input  [6:0] Number,
  output out_2,
  output out_3,
  output out_4,
  output out_5,
  output out_6,
  output out_7,
  output out_8
);


  assign out_2 = Number[0];
  assign out_3 = Number[1];
  assign out_4 = Number[2];
  assign out_5 = Number[3];
  assign out_6 = Number[4];
  assign out_7 = Number[5];
  assign out_8 = Number[6];
endmodule

module OpChooser (
  input  add,
  input  sub,
  input  \and ,
  input  \or ,
  input  mult,
  input  beq,
  input  jump,
  input  load,
  input  store,
  input  addi,
  output s3,
  output s2,
  output s1,
  output s0
);

  or or_1 (s3, addi, store, load);
  or or_2 (s2, jump, beq, mult, \or );
  or or_3 (s1, addi, jump, beq, \and , sub);
  or or_4 (s0, store, jump, mult, \and , add);
endmodule

// register
module Register (
  input  [4:0] rs,
  input  [31:0] in_rd,
  input  [4:0] rt,
  input  [4:0] rd,
  output [31:0] output_rs,
  output [31:0] output_rt
);

  wire Clock, comparator_1_eq, r0, r1, r2, r3, r4, r5, r6, r7, r8, r9, r10, r11, r12, r13, r14, r15, r16,
       r17, r18, r19, r20, r21, r22, r23, r24, r25, r26, r27, r28, r29, r30, r31;
  wire [31:0] i0, i1, i2, i3, i4, i5, i6, i7, i8, i9, i10, i11, i12, i13, i14, i15, i16, i17, i18, i19, i20,
       i21, i22, i23, i24, i25, i26, i27, i28, i29, i30, i31, o0, o1, o2, o3, o4, o5, o6, o7, o8, o9, o10,
       o11, o12, o13, o14, o15, o16, o17, o18, o19, o20, o21, o22, o23, o24, o25, o26, o27, o28, o29, o30,
       o31, preregister_1_output, preregister_2_output, preregister_3_output, preregister_4_output,
       preregister_5_output, preregister_6_p3, preregister_7_p3, preregister_8_p3, preregister_9_output,
       preregister_10_output, preregister_11_output, preregister_12_output, preregister_13_output,
       preregister_14_output, preregister_15_output, preregister_16_output, preregister_17_output,
       preregister_18_output, preregister_19_output, preregister_20_output, preregister_21_output,
       preregister_22_output, preregister_23_output, preregister_24_output, preregister_25_output,
       preregister_26_output, preregister_27_output, preregister_28_output, preregister_29_output,
       preregister_30_output, preregister_31_output, preregister_32_output;

  Clock clock_1 (.out(Clock));
  Multiplexer #(.select(5), .width(32), .enable("false")) multiplexer_1 (
    .in0(o0), .in1(o1), .in2(o2), .in3(o3), .in4(o4), .in5(o5), .in6(o6), .in7(o7), .in8(o8), .in9(o9),
    .in10(o10), .in11(o11), .in12(o12), .in13(o13), .in14(o14), .in15(o15), .in16(o16), .in17(o17),
    .in18(o18), .in19(o19), .in20(o20), .in21(o21), .in22(o22), .in23(o23), .in24(o24), .in25(o25),
    .in26(o26), .in27(o27), .in28(o28), .in29(o29), .in30(o30), .in31(o31), .out(output_rs), .sel(rs));
  Multiplexer #(.select(5), .width(32), .enable("false")) multiplexer_2 (
    .in0(o0), .in1(o1), .in2(o2), .in3(o3), .in4(o4), .in5(o5), .in6(o6), .in7(o7), .in8(o8), .in9(o9),
    .in10(o10), .in11(o11), .in12(o12), .in13(o13), .in14(o14), .in15(o15), .in16(o16), .in17(o17),
    .in18(o18), .in19(o19), .in20(o20), .in21(o21), .in22(o22), .in23(o23), .in24(o24), .in25(o25),
    .in26(o26), .in27(o27), .in28(o28), .in29(o29), .in30(o30), .in31(o31), .out(output_rt), .sel(rt));
  Register_part #(.width(32)) register_1 (.D(preregister_1_output), .Q(o0), .clk(Clock), .clr(r0));  // open: en
  preRegister preregister_1 (.\input (i0), .saved(o0), .\output (preregister_1_output));
  preRegister preregister_2 (.\input (i8), .saved(o8), .\output (preregister_2_output));
  Register_part #(.width(32)) register_2 (.D(preregister_2_output), .Q(o8), .clk(Clock), .clr(r8));  // open: en
  Register_part #(.width(32)) register_3 (.D(preregister_3_output), .Q(o16), .clk(Clock), .clr(r16));  // open: en
  preRegister preregister_3 (.\input (i16), .saved(o16), .\output (preregister_3_output));
  preRegister preregister_4 (.\input (i24), .saved(o24), .\output (preregister_4_output));
  Register_part #(.width(32)) register_4 (.D(preregister_4_output), .Q(o24), .clk(Clock), .clr(r24));  // open: en
  Demultiplexer #(.select(5), .width(32), .enable("false")) demultiplexer_1 (
    .out0(i0), .out1(i1), .out2(i2), .out3(i3), .out4(i4), .out5(i5), .out6(i6), .out7(i7), .out8(i8),
    .out9(i9), .out10(i10), .out11(i11), .out12(i12), .out13(i13), .out14(i14), .out15(i15), .out16(i16),
    .out17(i17), .out18(i18), .out19(i19), .out20(i20), .out21(i21), .out22(i22), .out23(i23), .out24(i24),
    .out25(i25), .out26(i26), .out27(i27), .out28(i28), .out29(i29), .out30(i30), .out31(i31), .in(in_rd),
    .sel(rd));
  preRegister preregister_5 (.\input (i1), .saved(o1), .\output (preregister_5_output));
  // preRegister preregister_6: pin names not known; wires that end beside it: o9, i9, preregister_6_p3
  // preRegister preregister_7: pin names not known; wires that end beside it: o17, i17, preregister_7_p3
  // preRegister preregister_8: pin names not known; wires that end beside it: o25, i25, preregister_8_p3
  preRegister preregister_9 (.\input (i2), .saved(o2), .\output (preregister_9_output));
  Register_part #(.width(32)) register_5 (.D(preregister_5_output), .Q(o1), .clk(Clock), .clr(r1));  // open: en
  preRegister preregister_10 (.\input (i10), .saved(o10), .\output (preregister_10_output));
  Register_part #(.width(32)) register_6 (.D(preregister_6_p3), .Q(o9), .clk(Clock), .clr(r9));  // open: en
  preRegister preregister_11 (.\input (i18), .saved(o18), .\output (preregister_11_output));
  Register_part #(.width(32)) register_7 (.D(preregister_7_p3), .Q(o17), .clk(Clock), .clr(r17));  // open: en
  preRegister preregister_12 (.\input (i26), .saved(o26), .\output (preregister_12_output));
  Register_part #(.width(32)) register_8 (.D(preregister_8_p3), .Q(o25), .clk(Clock), .clr(r25));  // open: en
  Comparator #(.width(32)) comparator_1 (.a(in_rd), .b({32{1'b0}}), .eq(comparator_1_eq));  // open: gt, lt
  Register_part #(.width(32)) register_9 (.D(preregister_9_output), .Q(o2), .clk(Clock), .clr(r2));  // open: en
  Register_part #(.width(32)) register_10 (.D(preregister_10_output), .Q(o10), .clk(Clock), .clr(r10));  // open: en
  Register_part #(.width(32)) register_11 (.D(preregister_11_output), .Q(o18), .clk(Clock), .clr(r18));  // open: en
  Register_part #(.width(32)) register_12 (.D(preregister_12_output), .Q(o26), .clk(Clock), .clr(r26));  // open: en
  Demultiplexer #(.select(5), .enable("false")) demultiplexer_2 (
    .out0(r0), .out1(r1), .out2(r2), .out3(r3), .out4(r4), .out5(r5), .out6(r6), .out7(r7), .out8(r8),
    .out9(r9), .out10(r10), .out11(r11), .out12(r12), .out13(r13), .out14(r14), .out15(r15), .out16(r16),
    .out17(r17), .out18(r18), .out19(r19), .out20(r20), .out21(r21), .out22(r22), .out23(r23), .out24(r24),
    .out25(r25), .out26(r26), .out27(r27), .out28(r28), .out29(r29), .out30(r30), .out31(r31),
    .in(comparator_1_eq), .sel(rd));
  preRegister preregister_13 (.\input (i3), .saved(o3), .\output (preregister_13_output));
  Register_part #(.width(32)) register_13 (.D(preregister_13_output), .Q(o3), .clk(Clock), .clr(r3));  // open: en
  preRegister preregister_14 (.\input (i11), .saved(o11), .\output (preregister_14_output));
  Register_part #(.width(32)) register_14 (.D(preregister_14_output), .Q(o11), .clk(Clock), .clr(r11));  // open: en
  Register_part #(.width(32)) register_15 (.D(preregister_15_output), .Q(o19), .clk(Clock), .clr(r19));  // open: en
  preRegister preregister_15 (.\input (i19), .saved(o19), .\output (preregister_15_output));
  Register_part #(.width(32)) register_16 (.D(preregister_16_output), .Q(o27), .clk(Clock), .clr(r27));  // open: en
  preRegister preregister_16 (.\input (i27), .saved(o27), .\output (preregister_16_output));
  Register_part #(.width(32)) register_17 (.D(preregister_17_output), .Q(o4), .clk(Clock), .clr(r4));  // open: en
  preRegister preregister_17 (.\input (i4), .saved(o4), .\output (preregister_17_output));
  Register_part #(.width(32)) register_18 (.D(preregister_18_output), .Q(o12), .clk(Clock), .clr(r12));  // open: en
  preRegister preregister_18 (.\input (i12), .saved(o12), .\output (preregister_18_output));
  Register_part #(.width(32)) register_19 (.D(preregister_19_output), .Q(o20), .clk(Clock), .clr(r20));  // open: en
  preRegister preregister_19 (.\input (i20), .saved(o20), .\output (preregister_19_output));
  preRegister preregister_20 (.\input (i28), .saved(o28), .\output (preregister_20_output));
  Register_part #(.width(32)) register_20 (.D(preregister_20_output), .Q(o28), .clk(Clock), .clr(r28));  // open: en
  preRegister preregister_21 (.\input (i5), .saved(o5), .\output (preregister_21_output));
  preRegister preregister_22 (.\input (i13), .saved(o13), .\output (preregister_22_output));
  preRegister preregister_23 (.\input (i21), .saved(o21), .\output (preregister_23_output));
  preRegister preregister_24 (.\input (i29), .saved(o29), .\output (preregister_24_output));
  preRegister preregister_25 (.\input (i6), .saved(o6), .\output (preregister_25_output));
  Register_part #(.width(32)) register_21 (.D(preregister_21_output), .Q(o5), .clk(Clock), .clr(r5));  // open: en
  preRegister preregister_26 (.\input (i14), .saved(o14), .\output (preregister_26_output));
  Register_part #(.width(32)) register_22 (.D(preregister_22_output), .Q(o13), .clk(Clock), .clr(r13));  // open: en
  preRegister preregister_27 (.\input (i22), .saved(o22), .\output (preregister_27_output));
  Register_part #(.width(32)) register_23 (.D(preregister_23_output), .Q(o21), .clk(Clock), .clr(r21));  // open: en
  preRegister preregister_28 (.\input (i30), .saved(o30), .\output (preregister_28_output));
  Register_part #(.width(32)) register_24 (.D(preregister_24_output), .Q(o29), .clk(Clock), .clr(r29));  // open: en
  Register_part #(.width(32)) register_25 (.D(preregister_25_output), .Q(o6), .clk(Clock), .clr(r6));  // open: en
  Register_part #(.width(32)) register_26 (.D(preregister_26_output), .Q(o14), .clk(Clock), .clr(r14));  // open: en
  Register_part #(.width(32)) register_27 (.D(preregister_27_output), .Q(o22), .clk(Clock), .clr(r22));  // open: en
  Register_part #(.width(32)) register_28 (.D(preregister_28_output), .Q(o30), .clk(Clock), .clr(r30));  // open: en
  Register_part #(.width(32)) register_29 (.D(preregister_29_output), .Q(o7), .clk(Clock), .clr(r7));  // open: en
  preRegister preregister_29 (.\input (i7), .saved(o7), .\output (preregister_29_output));
  Register_part #(.width(32)) register_30 (.D(preregister_30_output), .Q(o15), .clk(Clock), .clr(r15));  // open: en
  preRegister preregister_30 (.\input (i15), .saved(o15), .\output (preregister_30_output));
  Register_part #(.width(32)) register_31 (.D(preregister_31_output), .Q(o23), .clk(Clock), .clr(r23));  // open: en
  preRegister preregister_31 (.\input (i23), .saved(o23), .\output (preregister_31_output));
  preRegister preregister_32 (.\input (i31), .saved(o31), .\output (preregister_32_output));
  Register_part #(.width(32)) register_32 (.D(preregister_32_output), .Q(o31), .clk(Clock), .clr(r31));  // open: en
endmodule

module preRegister (
  input  [31:0] \input ,
  input  [31:0] saved,
  output [31:0] \output 
);

  wire comparator_1_eq;

  Comparator #(.width(32)) comparator_1 (.a({32{1'b0}}), .b(\input ), .eq(comparator_1_eq));  // open: gt, lt
  Multiplexer #(.width(32), .enable("false")) multiplexer_1 (
    .in0(\input ), .in1(saved), .out(\output ), .sel(comparator_1_eq));
endmodule

module TestCircuit (
  input  in_1,
  input  in_2,
  output out_3,
  output out_4
);

  wire clock_1_out, comparator_1_eq, comparator_2_eq, demultiplexer_1_out0, demultiplexer_1_out1,
       multiplexer_1_out;

  Demultiplexer #(.enable("false")) demultiplexer_1 (
    .out0(demultiplexer_1_out0), .out1(demultiplexer_1_out1), .in(in_1), .sel(in_2));
  Clock clock_1 (.out(clock_1_out));
  Register_part #(.width(1)) register_1 (
    .D(demultiplexer_1_out1), .Q(out_4), .clk(clock_1_out), .clr(comparator_1_eq));  // open: en
  Comparator #(.width(1)) comparator_1 (.a(in_1), .b(1'b0), .eq(comparator_1_eq));  // open: gt, lt
  Register_part #(.width(1)) register_2 (
    .D(multiplexer_1_out), .Q(out_3), .clk(clock_1_out), .clr(comparator_1_eq));  // open: en
  Comparator #(.width(1)) comparator_2 (.a(1'b0), .b(demultiplexer_1_out0), .eq(comparator_2_eq));  // open: gt, lt
  Multiplexer #(.enable("false")) multiplexer_1 (
    .in0(demultiplexer_1_out0), .in1(out_3), .out(multiplexer_1_out), .sel(comparator_2_eq));
endmodule

module ALU (
  input  [31:0] Dato1,
  input  [31:0] Dato2,
  input  [3:0] Opcode,
  output C,
  output V,
  output [31:0] Output
);

  wire [31:0] AU_output, lu_1_output, multiplexer_1_out, multiplexer_2_out, not_1_out, not_2_out;

  assign not_1_out = ~Dato1;  // NOT_Gate not_1, 32 bits wide
  Multiplexer #(.width(32), .enable("false")) multiplexer_1 (
    .in0(Dato2), .in1(not_2_out), .out(multiplexer_1_out), .sel(Opcode[1]));
  assign not_2_out = ~Dato2;  // NOT_Gate not_2, 32 bits wide
  Multiplexer #(.width(32), .enable("false")) multiplexer_2 (
    .in0(Dato1), .in1(not_1_out), .out(multiplexer_2_out), .sel(Opcode[0]));
  AU AU (
    .CIN(Opcode[2]), .Dato1(multiplexer_2_out), .Dato2(multiplexer_1_out), .Output(AU_output), .COUT(C),
    .Overflow(V));
  LU lu_1 (.Dato1(Dato1), .Dato2(multiplexer_1_out), .f2(Opcode[2]), .f0(Opcode[0]), .Output(lu_1_output));
  Multiplexer #(.width(32), .enable("false")) multiplexer_3 (
    .in0(AU_output), .in1(lu_1_output), .out(Output), .sel(Opcode[3]));
endmodule

module Unidad_Control (
  input  [5:0] op_in,
  output RegDist,
  output ALUSrc,
  output MemToReg,
  output RegWrite,
  output MemReed,
  output MemWrite,
  output Branch,
  output [1:0] AluOP
);

  and and_1 (AluOP[1], ~op_in[5], ~op_in[1], ~op_in[2], ~op_in[3], ~op_in[4], ~op_in[0]);  // AND_Gate
  and and_2 (MemReed, op_in[5], ~op_in[1], ~op_in[2], ~op_in[3], op_in[4], op_in[0]);  // AND_Gate
  and and_3 (MemWrite, op_in[5], ~op_in[1], op_in[2], ~op_in[3], op_in[4], op_in[0]);  // AND_Gate
  and and_4 (AluOP[0], ~op_in[5], ~op_in[1], ~op_in[2], op_in[3], ~op_in[4], ~op_in[0]);  // AND_Gate
  or or_1 (ALUSrc, MemReed, MemWrite);
  or or_2 (RegWrite, AluOP[1], MemReed);

  assign Branch = AluOP[0];
  assign MemToReg = MemReed;
  assign RegDist = AluOP[1];
endmodule

module ALU_Control (
  input  [1:0] in_1,
  input  [5:0] funct,
  output [2:0] out_3
);

  wire and_1_out, or_1_out;

  or or_1 (or_1_out, funct[3], funct[0]);
  and and_1 (and_1_out, in_1[1], funct[1]);
  and and_2 (out_3[2], in_1[1], or_1_out);
  or or_2 (out_3[0], in_1[0], and_1_out);
  or or_3 (out_3[1], in_1[1], funct[2]);
endmodule

module AU (
  input  CIN,
  input  [31:0] Dato1,
  input  [31:0] Dato2,
  output [31:0] Output,
  output COUT,
  output Overflow
);

  wire adder_1_cout, adder_2_cout, adder_3_cout, adder_4_cout, adder_5_cout, adder_6_cout, adder_7_cout,
       adder_8_cout, adder_9_cout, adder_10_cout, adder_11_cout, adder_12_cout, adder_13_cout, adder_14_cout,
       adder_15_cout, adder_16_cout, adder_17_cout, adder_18_cout, adder_19_cout, adder_20_cout,
       adder_21_cout, adder_22_cout, adder_23_cout, adder_24_cout, adder_25_cout, adder_26_cout,
       adder_27_cout, adder_28_cout, adder_29_cout, adder_30_cout, adder_31_cout;

  Adder #(.width(1)) adder_1 (.a(Dato1[0]), .b(Dato2[0]), .out(Output[0]), .cin(CIN), .cout(adder_1_cout));
  Adder #(.width(1)) adder_2 (.a(Dato1[1]), .b(Dato2[1]), .out(Output[1]), .cin(adder_1_cout), .cout(adder_2_cout));
  Adder #(.width(1)) adder_3 (.a(Dato1[2]), .b(Dato2[2]), .out(Output[2]), .cin(adder_2_cout), .cout(adder_3_cout));
  Adder #(.width(1)) adder_4 (.a(Dato1[3]), .b(Dato2[3]), .out(Output[3]), .cin(adder_3_cout), .cout(adder_4_cout));
  Adder #(.width(1)) adder_5 (.a(Dato1[4]), .b(Dato2[4]), .out(Output[4]), .cin(adder_4_cout), .cout(adder_5_cout));
  Adder #(.width(1)) adder_6 (.a(Dato1[5]), .b(Dato2[5]), .out(Output[5]), .cin(adder_5_cout), .cout(adder_6_cout));
  Adder #(.width(1)) adder_7 (.a(Dato1[6]), .b(Dato2[6]), .out(Output[6]), .cin(adder_6_cout), .cout(adder_7_cout));
  Adder #(.width(1)) adder_8 (.a(Dato1[7]), .b(Dato2[7]), .out(Output[7]), .cin(adder_7_cout), .cout(adder_8_cout));
  Adder #(.width(1)) adder_9 (.a(Dato1[8]), .b(Dato2[8]), .out(Output[8]), .cin(adder_8_cout), .cout(adder_9_cout));
  Adder #(.width(1)) adder_10 (.a(Dato1[9]), .b(Dato2[9]), .out(Output[9]), .cin(adder_9_cout), .cout(adder_10_cout));
  Adder #(.width(1)) adder_11 (
    .a(Dato1[10]), .b(Dato2[10]), .out(Output[10]), .cin(adder_10_cout), .cout(adder_11_cout));
  Adder #(.width(1)) adder_12 (
    .a(Dato1[11]), .b(Dato2[11]), .out(Output[11]), .cin(adder_11_cout), .cout(adder_12_cout));
  Adder #(.width(1)) adder_13 (
    .a(Dato1[12]), .b(Dato2[12]), .out(Output[12]), .cin(adder_12_cout), .cout(adder_13_cout));
  Adder #(.width(1)) adder_14 (
    .a(Dato1[13]), .b(Dato2[13]), .out(Output[13]), .cin(adder_13_cout), .cout(adder_14_cout));
  Adder #(.width(1)) adder_15 (
    .a(Dato1[14]), .b(Dato2[14]), .out(Output[14]), .cin(adder_14_cout), .cout(adder_15_cout));
  Adder #(.width(1)) adder_16 (
    .a(Dato1[15]), .b(Dato2[15]), .out(Output[15]), .cin(adder_15_cout), .cout(adder_16_cout));
  Adder #(.width(1)) adder_17 (
    .a(Dato1[16]), .b(Dato2[16]), .out(Output[16]), .cin(adder_16_cout), .cout(adder_17_cout));
  Adder #(.width(1)) adder_18 (
    .a(Dato1[17]), .b(Dato2[17]), .out(Output[17]), .cin(adder_17_cout), .cout(adder_18_cout));
  Adder #(.width(1)) adder_19 (
    .a(Dato1[18]), .b(Dato2[18]), .out(Output[18]), .cin(adder_18_cout), .cout(adder_19_cout));
  Adder #(.width(1)) adder_20 (
    .a(Dato1[19]), .b(Dato2[19]), .out(Output[19]), .cin(adder_19_cout), .cout(adder_20_cout));
  Adder #(.width(1)) adder_21 (
    .a(Dato1[20]), .b(Dato2[20]), .out(Output[20]), .cin(adder_20_cout), .cout(adder_21_cout));
  Adder #(.width(1)) adder_22 (
    .a(Dato1[21]), .b(Dato2[21]), .out(Output[21]), .cin(adder_21_cout), .cout(adder_22_cout));
  Adder #(.width(1)) adder_23 (
    .a(Dato1[22]), .b(Dato2[22]), .out(Output[22]), .cin(adder_22_cout), .cout(adder_23_cout));
  Adder #(.width(1)) adder_24 (
    .a(Dato1[23]), .b(Dato2[23]), .out(Output[23]), .cin(adder_23_cout), .cout(adder_24_cout));
  Adder #(.width(1)) adder_25 (
    .a(Dato1[24]), .b(Dato2[24]), .out(Output[24]), .cin(adder_24_cout), .cout(adder_25_cout));
  Adder #(.width(1)) adder_26 (
    .a(Dato1[25]), .b(Dato2[25]), .out(Output[25]), .cin(adder_25_cout), .cout(adder_26_cout));
  Adder #(.width(1)) adder_27 (
    .a(Dato1[26]), .b(Dato2[26]), .out(Output[26]), .cin(adder_26_cout), .cout(adder_27_cout));
  Adder #(.width(1)) adder_28 (
    .a(Dato1[27]), .b(Dato2[27]), .out(Output[27]), .cin(adder_27_cout), .cout(adder_28_cout));
  Adder #(.width(1)) adder_29 (
    .a(Dato1[28]), .b(Dato2[28]), .out(Output[28]), .cin(adder_28_cout), .cout(adder_29_cout));
  Adder #(.width(1)) adder_30 (
    .a(Dato1[29]), .b(Dato2[29]), .out(Output[29]), .cin(adder_29_cout), .cout(adder_30_cout));
  Adder #(.width(1)) adder_31 (
    .a(Dato1[30]), .b(Dato2[30]), .out(Output[30]), .cin(adder_30_cout), .cout(adder_31_cout));
  Adder #(.width(1)) adder_32 (.a(Dato1[31]), .b(Dato2[31]), .out(Output[31]), .cin(adder_31_cout), .cout(COUT));
  xor xor_1 (Overflow, COUT, adder_31_cout);
endmodule

module LU (
  input  [31:0] Dato1,
  input  [31:0] Dato2,
  input  f2,
  input  f0,
  output [31:0] Output
);

  wire [31:0] and_1_out, or_1_out, xor_1_out;

  assign and_1_out = Dato1 & Dato2;  // AND_Gate and_1, 32 bits wide
  assign or_1_out = Dato1 | Dato2;  // OR_Gate or_1, 32 bits wide
  assign xor_1_out = Dato1 ^ Dato2;  // XOR_Gate xor_1, 32 bits wide
  Multiplexer #(.select(2), .width(32), .enable("false")) multiplexer_1 (
    .in0(and_1_out), .in1(or_1_out), .in2(xor_1_out), .in3(Dato2), .out(Output), .sel({f2, f0}));
endmodule
